# Fritzing sketch complete-breadboard (saved by Fritzing 0.9.10b)
breadboards: 1

parts:
  Mod1 = Raspberry Pi Pico
  LED1 = LED - 3mm [color="Red (633nm)" current=0.030 package="3 mm [THT]"]
  R1 = Resistor [tolerance=±5% resistance=220 package="1206 [SMD]"]
  RE1 = KY-040 Rotary encoder [package=THT]
  LED2 = LED - 3mm [color="Blue (505nm)" current=0.030 package="3 mm [THT]"]
  R2 = Resistor [tolerance=±5% resistance=220 package="1206 [SMD]"]
  OLED_I2C1 = OLED 128x64 I2C Monochrome Display

nets:
  GND: Mod1.pin_3, Mod1.pin_8, Mod1.pin_13, Mod1.pin_18, Mod1.pin_23, Mod1.pin_28, Mod1.pin_33, Mod1.pin_38, LED1.cathode, RE1.GND, LED2.cathode, OLED_I2C1.GND
  N1: Mod1.pin_6, OLED_I2C1.SCK
  N2: Mod1.pin_7, OLED_I2C1.SDA
  N3: Mod1.pin_10, RE1.SW
  N4: Mod1.pin_11, RE1.CLK
  N5: Mod1.pin_12, RE1.DT
  N6: Mod1.pin_19, R2.Pin_0
  N7: Mod1.pin_20, R1.Pin_0
  VCC: Mod1.pin_37, RE1.Vcc, OLED_I2C1.VDD
  N8: LED1.anode, R1.Pin_1
  N9: LED2.anode, R2.Pin_1

custom parts:
  Raspberry Pi Pico: Raspberry Pi Pico. Based around the RP2040 microcontroller the Pico is a low cost microcontroller device bringing Raspberry Pi quality, cost, and easy of use to the microcontroller space. Jan 2021, Split part in to two versions: tht (this one) and SMD. This one will drill holes for a .1 in header in pcb to allow plugging in the module as well as providing pads to solder the module to the top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
  KY-040 Rotary encoder: KY-040 Rotary Encoder with switch on breakout borad from AZ Delivery
